# Fritzing sketch DroneSketch (saved by Fritzing 0.9.2b)
breadboards: 1

parts:
  Part1 = Arduino Mega 2560 (Rev3)  # not connected
  Part2 = IMU Digital Combo Board 6DOF  # not connected
  920KV_Motor1 = DJI 920 KV Motor
  920KV_Motor2 = DJI 920 KV Motor
  920KV_Motor3 = DJI 920 KV Motor
  920KV_Motor4 = DJI 920 KV Motor
  DJI_ESC_30A1 = DJI 30A ESC
  Part4 = Logic Level Converter  # not connected
  Part5 = SRF05 Ultrasonic Rangefinder  # not connected
  U1 = XBEE-1 [package=xbee-1]  # not connected
  DJI_ESC_30A2 = DJI 30A ESC
  DJI_ESC_30A3 = DJI 30A ESC
  DJI_ESC_30A4 = DJI 30A ESC
  U2 = LIPO-2000mAh [package=lipo-2000]  # not connected
  Part3 = Barometric Pressure Sensor - BMP085 Breakout  # not connected

nets:
  N1: 920KV_Motor1.w, DJI_ESC_30A1.W
  N2: 920KV_Motor1.v, DJI_ESC_30A1.U, DJI_ESC_30A1.GND
  N3: 920KV_Motor1.u, DJI_ESC_30A1.V
  N4: 920KV_Motor2.w, DJI_ESC_30A2.W
  N5: 920KV_Motor2.v, DJI_ESC_30A2.U
  N6: 920KV_Motor2.u, DJI_ESC_30A2.V
  N7: 920KV_Motor3.w, DJI_ESC_30A3.W
  N8: 920KV_Motor3.v, DJI_ESC_30A3.U
  N9: 920KV_Motor3.u, DJI_ESC_30A3.V
  N10: 920KV_Motor4.w, DJI_ESC_30A4.W
  N11: 920KV_Motor4.v, DJI_ESC_30A4.U
  N12: 920KV_Motor4.u, DJI_ESC_30A4.V

custom parts:
  DJI 920 KV Motor: DJI Brushless Outrunner 2212/920K Motor F330-550
