# Fritzing sketch DroneSketch (saved by Fritzing 0.9.2b)

parts:
  Part1 = Arduino Mega 2560 (Rev3)
  Part2 = IMU Digital Combo Board 6DOF
  920KV_Motor1 = DJI 920 KV Motor
  920KV_Motor2 = DJI 920 KV Motor
  920KV_Motor3 = DJI 920 KV Motor
  920KV_Motor4 = DJI 920 KV Motor
  Part4 = Logic Level Converter
  Part5 = SRF05 Ultrasonic Rangefinder
  U1 = XBEE-1 [package=xbee-1]
  DJI_ESC_30A2 = DJI 30A ESC
  DJI_ESC_30A3 = DJI 30A ESC
  DJI_ESC_30A4 = DJI 30A ESC
  U2 = LIPO-2000mAh [package=lipo-2000]
  Part3 = Barometric Pressure Sensor - BMP085 Breakout
  DJI_ESC_30A5 = DJI 30A ESC

nets:
  N1: Part1.D21/SCL, Part4.RX2_HV
  N2: Part1.D20/SDA, Part4.TX2_HV
  N3: Part1.D19/RX1, Part4.TX_HV
  N4: Part1.D18/TX1, Part4.RX_HV
  N5: Part1.D17_PWM/RX2, U1.DIN
  N6: Part1.D16_PWM/TX2, U1.DOUT
  N7: Part1.D10_PWM, DJI_ESC_30A4.DATA
  N8: Part1.D9_PWM, DJI_ESC_30A3.DATA
  N9: Part1.D8_PWM, DJI_ESC_30A2.DATA
  3V3: Part1.3V3, Part4.LV, Part3.VCC
  5V: Part1.5V, Part2.3.3V, Part5.VCC, U1.VDD
  GND: Part1.GND, Part2.GND, Part4.GND, U1.GND, DJI_ESC_30A2.GND, DJI_ESC_30A3.GND, DJI_ESC_30A4.GND, Part3.GND, DJI_ESC_30A5.GND
  VIN: Part1.VIN, Part5.GND
  N10: Part1.D2_PWM, Part5.Trig
  N11: Part1.D3_PWM, Part5.Echo
  N12: Part1.D7_PWM, DJI_ESC_30A5.DATA
  N13: Part2.SDA, Part4.RX_LV
  N14: Part2.SCL, Part4.TX_LV
  N15: 920KV_Motor1.w, DJI_ESC_30A5.W
  N16: 920KV_Motor1.v, DJI_ESC_30A5.U
  N17: 920KV_Motor1.u, DJI_ESC_30A5.V
  N18: 920KV_Motor2.w, DJI_ESC_30A2.W
  N19: 920KV_Motor2.v, DJI_ESC_30A2.U
  N20: 920KV_Motor2.u, DJI_ESC_30A2.V
  N21: 920KV_Motor3.w, DJI_ESC_30A3.W
  N22: 920KV_Motor3.v, DJI_ESC_30A3.U
  N23: 920KV_Motor3.u, DJI_ESC_30A3.V
  N24: 920KV_Motor4.w, DJI_ESC_30A4.W
  N25: 920KV_Motor4.v, DJI_ESC_30A4.U
  N26: 920KV_Motor4.u, DJI_ESC_30A4.V
  N27: Part4.TX2_LV, Part3.SDA
  N28: Part4.RX2_LV, Part3.SCL
  N29: DJI_ESC_30A2.GROUND, DJI_ESC_30A3.GROUND, DJI_ESC_30A4.GROUND, U2.-, DJI_ESC_30A5.GROUND
  +12V: DJI_ESC_30A2.+12V, DJI_ESC_30A3.+12V, DJI_ESC_30A4.+12V, U2.+, DJI_ESC_30A5.+12V

custom parts:
  DJI 920 KV Motor: DJI Brushless Outrunner 2212/920K Motor F330-550
